# Fritzing sketch Breadboard_Circuit (saved by Fritzing 0.9.9b)
breadboards: 1

parts:
  IC1 = ULN2003A [package="SO16 [SMD]"]
  SM1 = 28BYJ-48 Stepper Motor [part_number=28BYJ-48]
  Part1 = Arduino Uno (Rev3)
  LED1 = smd LED [color="Red (633nm)" package="0805 [SMD]"]
  LED2 = smd LED [color="Red (633nm)" package="0805 [SMD]"]
  LED3 = smd LED [color="Red (633nm)" package="0805 [SMD]"]
  LED4 = smd LED [color="Red (633nm)" package="0805 [SMD]"]
  R1 = Resistor [tolerance=±0.5% resistance=1k package=THT]
  R2 = Resistor [tolerance=±0.5% resistance=1k package=THT]
  R3 = Resistor [tolerance=±0.5% resistance=1k package=THT]
  R4 = Resistor [tolerance=±0.5% resistance=1k package=THT]
  J2 = Screw terminal - 2 pins [package=THT]

nets:
  N1: IC1.In_5, SM1.orange-pin, R1.Pin_1
  N2: IC1.In_6, SM1.yellow-pin, R2.Pin_1
  N3: IC1.In_7, SM1.pink-pin, R3.Pin_1
  N4: IC1.0V, SM1.blue-pin, R4.Pin_1
  N5: IC1.COM_-_Common, Part1.D11_PWM/MOSI
  N6: IC1.Out_7, Part1.D10_PWM/SS
  N7: IC1.Out_6, Part1.D9_PWM
  N8: IC1.Out_5, Part1.D8
  N9: IC1.Out_1, Part1.GND, J2.pin1
  N10: SM1.red-pin, J2.pin2
  N11: LED1.cathode, R2.Pin_0
  N12: LED1.anode, LED2.anode, LED3.anode, LED4.anode
  N13: LED2.cathode, R1.Pin_0
  N14: LED3.cathode, R4.Pin_0
  N15: LED4.cathode, R3.Pin_0

notes:
  12V DC Power Supply

custom parts:
  28BYJ-48 Stepper Motor: Unipolar Stepper Motor 28BYJ-48 Top coil - pink & orange Bottom coil - blue & yellow Common rail - red Connector pins: blue - pink - yellow - orange - red
